// Logisim project final_cpu.circ as structural Verilog: 10 circuits, main circuit main
module main (
  input  in_1,
  input  in_2,
  input  in_3,
  input  in_4,
  input  Reading,
  input  Address,
  input  in_7,
  input  in_8,
  output Neg_status,
  output Zero_status,
  output Mag_Overflow,
  output Signed_Overflow
);

  wire adder_1_out_5, adder_1_out_6, adder_1_out_7, alu_1_magnitude_overflow_status, alu_1_neg_status,
       alu_1_out1, alu_1_out2, alu_1_out3, alu_1_out4, alu_1_signed_overflow_satus, alu_1_zero_status,
       and_1_out, and_2_out, and_3_out, and_4_out, and_5_out, and_6_out, and_7_out, and_8_out, and_9_out,
       and_10_out, and_11_out, and_12_out, and_13_out, and_14_out, and_15_out, and_16_out, and_17_out,
       and_18_out, and_19_out, and_20_out, and_21_out, and_22_out, and_23_out, and_24_out, and_25_out,
       and_26_out, and_27_out, and_28_out, and_29_out, and_30_out, and_31_out, and_32_out, and_33_out,
       and_34_out, and_35_out, and_36_out, and_37_out, big_man_cu_1_aluop, big_man_cu_1_halt,
       big_man_cu_1_incr_pc, big_man_cu_1_memread, big_man_cu_1_memwrite, big_man_cu_1_pcoram,
       big_man_cu_1_ramtoir, big_man_cu_1_regread, big_man_cu_1_regwrite, big_man_cu_1_reset_ir,
       big_man_cu_1_setaddress, clock_1_out, d_ff_1_q, d_ff_2_q, d_ff_3_q, d_ff_4_q, d_ff_5_q, d_ff_6_q,
       d_ff_7_q, data_ram_1_output_1, data_ram_1_output_2, data_ram_1_output_3, data_ram_1_output_4,
       instructions_ram_1_output_1, instructions_ram_1_output_2, instructions_ram_1_output_3,
       instructions_ram_1_output_4, multiplexer_1_out_4, multiplexer_2_out_4, multiplexer_3_out_4,
       multiplexer_4_out_4, multiplexer_6_out_4, multiplexer_7_out_4, multiplexer_8_out_4,
       multiplexer_9_out_4, multiplexer_10_out_4, multiplexer_11_out_4, multiplexer_12_out_4,
       multiplexer_13_out_4, multiplexer_14_out_4, multiplexerx4_1_out1, multiplexerx4_1_out2,
       multiplexerx4_1_out3, multiplexerx4_1_out4, multiplexerx4_2_out1, multiplexerx4_2_out2,
       multiplexerx4_2_out3, multiplexerx4_2_out4, nand_1_out, not_1_out, not_2_out, or_1_out, or_2_out,
       or_3_out, or_4_out, or_5_out, or_6_out, register_blck_1_output1, register_blck_1_output1_2,
       register_blck_1_output2, register_blck_1_output2_2, register_blck_1_output3,
       register_blck_1_output3_2, register_blck_1_output4, register_blck_1_output4_2, xor_1_out, xor_2_out;

  and and_1 (and_1_out, adder_1_out_7, big_man_cu_1_incr_pc);
  and and_2 (and_2_out, adder_1_out_6, big_man_cu_1_incr_pc);
  and and_3 (and_3_out, adder_1_out_5, big_man_cu_1_incr_pc);
  D_Flip_Flop #(.trigger("falling")) d_ff_1 (.D(and_3_out), .clk(and_8_out), .Q(d_ff_1_q));  // open: Qn, preset, reset
  D_Flip_Flop #(.trigger("falling")) d_ff_2 (.D(and_2_out), .clk(and_8_out), .Q(d_ff_2_q));  // open: Qn, preset, reset
  and and_4 (and_4_out, d_ff_1_q, big_man_cu_1_pcoram);
  Multiplexer multiplexer_1 (.in_1(1'b0), .in_2(clock_1_out), .in_3(big_man_cu_1_halt), .out_4(multiplexer_1_out_4));
  D_Flip_Flop #(.trigger("falling")) d_ff_3 (.D(and_1_out), .clk(and_8_out), .Q(d_ff_3_q));  // open: Qn, preset, reset
  and and_5 (and_5_out, d_ff_3_q, big_man_cu_1_pcoram);
  and and_6 (and_6_out, d_ff_2_q, big_man_cu_1_pcoram);
  adder adder_1 (
    .in_1(and_4_out), .in_2(and_6_out), .in_3(and_5_out), .out_5(adder_1_out_5), .out_6(adder_1_out_6),
    .out_7(adder_1_out_7));  // open: out_4
  and and_7 (and_7_out, multiplexer_1_out_4, Reading);
  and and_8 (and_8_out, and_7_out, big_man_cu_1_incr_pc);
  big_man_CU big_man_cu_1 (
    .in_4(d_ff_4_q), .in_3(d_ff_5_q), .in_2(d_ff_6_q), .in_1(d_ff_7_q), .RegRead(big_man_cu_1_regread),
    .SetAddress(big_man_cu_1_setaddress), .memWrite(big_man_cu_1_memwrite), .RegWrite(big_man_cu_1_regwrite),
    .memRead(big_man_cu_1_memread), .incr_pc(big_man_cu_1_incr_pc), .PCoRAM(big_man_cu_1_pcoram),
    .RAMtoIR(big_man_cu_1_ramtoir), .ALUop(big_man_cu_1_aluop), .HALT(big_man_cu_1_halt), .in_5(and_7_out),
    .reset_ir(big_man_cu_1_reset_ir));
  Clock clock_1 (.out(clock_1_out));
  Instructions_ram instructions_ram_1 (
    .Output_1(instructions_ram_1_output_1), .Output_2(instructions_ram_1_output_2),
    .Output_3(instructions_ram_1_output_3), .Output_4(instructions_ram_1_output_4), .Mode(Reading),
    .Address_1(multiplexer_4_out_4), .Address_2(multiplexer_3_out_4), .Address_3(multiplexer_2_out_4),
    .Data_1(in_4), .Data_2(in_3), .Data_3(in_2), .Data_4(in_1), .Clock(or_1_out));
  or or_1 (or_1_out, and_9_out, and_7_out);
  and and_9 (and_9_out, ~Reading, multiplexer_1_out_4);  // AND_Gate
  Multiplexer multiplexer_2 (.in_1(and_4_out), .in_2(Address), .in_3(Reading), .out_4(multiplexer_2_out_4));
  Multiplexer multiplexer_3 (.in_1(and_6_out), .in_2(in_7), .in_3(Reading), .out_4(multiplexer_3_out_4));
  Multiplexer multiplexer_4 (.in_1(and_5_out), .in_2(in_8), .in_3(Reading), .out_4(multiplexer_4_out_4));
  and and_10 (and_10_out, instructions_ram_1_output_1, big_man_cu_1_ramtoir);
  and and_11 (and_11_out, instructions_ram_1_output_2, big_man_cu_1_ramtoir);
  and and_12 (and_12_out, instructions_ram_1_output_3, big_man_cu_1_ramtoir);
  and and_13 (and_13_out, instructions_ram_1_output_4, big_man_cu_1_ramtoir);
  nand nand_1 (nand_1_out, and_7_out, big_man_cu_1_ramtoir);
  D_Flip_Flop d_ff_4 (
    .D(and_13_out), .clk(nand_1_out), .Q(d_ff_4_q), .reset(big_man_cu_1_reset_ir));  // open: Qn, preset
  D_Flip_Flop d_ff_5 (
    .D(and_12_out), .clk(nand_1_out), .Q(d_ff_5_q), .reset(big_man_cu_1_reset_ir));  // open: Qn, preset
  and and_14 (and_14_out, ~d_ff_4_q, ~d_ff_5_q);  // AND_Gate
  and and_15 (and_15_out, ~d_ff_4_q, d_ff_5_q);  // AND_Gate
  and and_16 (and_16_out, d_ff_4_q, ~d_ff_5_q);  // AND_Gate
  and and_17 (and_17_out, d_ff_4_q, d_ff_5_q);
  D_Flip_Flop d_ff_6 (
    .D(and_11_out), .clk(nand_1_out), .Q(d_ff_6_q), .reset(big_man_cu_1_reset_ir));  // open: Qn, preset
  D_Flip_Flop d_ff_7 (
    .D(and_10_out), .clk(nand_1_out), .Q(d_ff_7_q), .reset(big_man_cu_1_reset_ir));  // open: Qn, preset
  and and_18 (and_18_out, d_ff_6_q, and_14_out);  // AND_Gate
  and and_19 (and_19_out, d_ff_7_q, and_14_out);  // AND_Gate
  and and_20 (and_20_out, ~d_ff_6_q, and_15_out);  // AND_Gate
  and and_21 (and_21_out, d_ff_7_q, and_15_out);  // AND_Gate
  and and_22 (and_22_out, d_ff_6_q, and_16_out);
  and and_23 (and_23_out, d_ff_7_q, and_16_out);
  and and_24 (and_24_out, d_ff_6_q, and_17_out);
  and and_25 (and_25_out, d_ff_7_q, and_17_out);
  not not_1 (not_1_out, and_20_out);
  xor xor_1 (xor_1_out, and_24_out, and_25_out);
  or or_2 (or_2_out, and_23_out, and_25_out);
  Multiplexer multiplexer_5 (.in_1(not_1_out), .in_2(and_18_out), .in_3(d_ff_5_q));  // open: out_4
  or or_3 (or_3_out, and_22_out, and_24_out);
  xor xor_2 (xor_2_out, and_22_out, and_23_out);
  D_Flip_Flop d_ff_8 (
    .D(alu_1_signed_overflow_satus), .clk(and_7_out), .Q(Signed_Overflow));  // open: Qn, preset, reset
  or or_4 (or_4_out, and_16_out, and_17_out);
  Multiplexer multiplexer_6 (.in_1(xor_2_out), .in_2(xor_1_out), .in_3(and_16_out), .out_4(multiplexer_6_out_4));
  D_Flip_Flop d_ff_9 (.D(alu_1_neg_status), .clk(and_7_out), .Q(Neg_status));  // open: Qn, preset, reset
  D_Flip_Flop d_ff_10 (.D(alu_1_zero_status), .clk(and_7_out), .Q(Zero_status));  // open: Qn, preset, reset
  D_Flip_Flop d_ff_11 (
    .D(alu_1_magnitude_overflow_status), .clk(and_7_out), .Q(Mag_Overflow));  // open: Qn, preset, reset
  Register_blck register_blck_1 (
    .Load(big_man_cu_1_regwrite), .Save(big_man_cu_1_regread), .output3(register_blck_1_output3),
    .output2(register_blck_1_output2), .Data_input4(multiplexer_11_out_4),
    .Data_input3(multiplexer_12_out_4), .Data_input2(multiplexer_13_out_4),
    .Data_input1(multiplexer_14_out_4), .output1(register_blck_1_output1), .output4(register_blck_1_output4),
    .output4_2(register_blck_1_output4_2), .output3_2(register_blck_1_output3_2),
    .output2_2(register_blck_1_output2_2), .output1_2(register_blck_1_output1_2), .register_choice(d_ff_6_q),
    .Bothregister_flag(multiplexer_6_out_4), .Clock(and_7_out));
  not not_2 (not_2_out, and_16_out);
  Multiplexer multiplexer_7 (
    .in_1(register_blck_1_output4_2), .in_2(register_blck_1_output4), .in_3(d_ff_6_q),
    .out_4(multiplexer_7_out_4));
  Multiplexer multiplexer_8 (
    .in_1(register_blck_1_output3_2), .in_2(register_blck_1_output3), .in_3(d_ff_6_q),
    .out_4(multiplexer_8_out_4));
  Multiplexer multiplexer_9 (
    .in_1(register_blck_1_output2_2), .in_2(register_blck_1_output2), .in_3(d_ff_6_q),
    .out_4(multiplexer_9_out_4));
  Multiplexer multiplexer_10 (
    .in_1(register_blck_1_output1_2), .in_2(register_blck_1_output1), .in_3(d_ff_6_q),
    .out_4(multiplexer_10_out_4));
  multiplexerX4 multiplexerx4_1 (
    .out1_1(register_blck_1_output1), .out1_2(register_blck_1_output2), .out1_3(register_blck_1_output3),
    .out1_4(register_blck_1_output4), .out2_1(register_blck_1_output1_2), .out2_2(register_blck_1_output2_2),
    .out2_3(register_blck_1_output3_2), .out2_4(register_blck_1_output4_2), .out4(multiplexerx4_1_out4),
    .out3(multiplexerx4_1_out3), .out2(multiplexerx4_1_out2), .out1(multiplexerx4_1_out1), .in_9(or_2_out));
  multiplexerX4 multiplexerx4_2 (
    .out1_1(register_blck_1_output1), .out1_2(register_blck_1_output2), .out1_3(register_blck_1_output3),
    .out1_4(register_blck_1_output4), .out2_1(register_blck_1_output1_2), .out2_2(register_blck_1_output2_2),
    .out2_3(register_blck_1_output3_2), .out2_4(register_blck_1_output4_2), .out4(multiplexerx4_2_out4),
    .out3(multiplexerx4_2_out3), .out2(multiplexerx4_2_out2), .out1(multiplexerx4_2_out1), .in_9(or_3_out));
  or or_5 (or_5_out, big_man_cu_1_setaddress, big_man_cu_1_memwrite, big_man_cu_1_regread);
  and and_26 (and_26_out, multiplexer_7_out_4, or_5_out);
  and and_27 (and_27_out, multiplexer_8_out_4, or_5_out);
  and and_28 (and_28_out, multiplexer_9_out_4, or_5_out);
  and and_29 (and_29_out, multiplexer_10_out_4, or_5_out);
  and and_30 (and_30_out, multiplexerx4_1_out4, big_man_cu_1_aluop);
  and and_31 (and_31_out, multiplexerx4_1_out3, big_man_cu_1_aluop);
  and and_32 (and_32_out, multiplexerx4_1_out2, big_man_cu_1_aluop);
  and and_33 (and_33_out, multiplexerx4_1_out1, big_man_cu_1_aluop);
  and and_34 (and_34_out, multiplexerx4_2_out4, big_man_cu_1_aluop);
  and and_35 (and_35_out, multiplexerx4_2_out3, big_man_cu_1_aluop);
  and and_36 (and_36_out, multiplexerx4_2_out2, big_man_cu_1_aluop);
  and and_37 (and_37_out, multiplexerx4_2_out1, big_man_cu_1_aluop);
  ALU alu_1 (
    .Clock(and_7_out), .L_input4(and_34_out), .L_input3(and_35_out), .L_input2(and_36_out),
    .L_input1(and_37_out), .R_input4(and_30_out), .R_input3(and_31_out), .R_input2(and_32_out),
    .R_input1(and_33_out), .Add_Sub(not_2_out), .Neg_status(alu_1_neg_status),
    .Zero_status(alu_1_zero_status), .Magnitude_Overflow_status(alu_1_magnitude_overflow_status),
    .Signed_Overflow_satus(alu_1_signed_overflow_satus), .out4(alu_1_out4), .out3(alu_1_out3),
    .out2(alu_1_out2), .out1(alu_1_out1));
  Multiplexer multiplexer_11 (
    .in_1(alu_1_out4), .in_2(data_ram_1_output_4), .in_3(or_4_out), .out_4(multiplexer_11_out_4));
  Multiplexer multiplexer_12 (
    .in_1(alu_1_out3), .in_2(data_ram_1_output_3), .in_3(or_4_out), .out_4(multiplexer_12_out_4));
  Multiplexer multiplexer_13 (
    .in_1(alu_1_out2), .in_2(data_ram_1_output_2), .in_3(or_4_out), .out_4(multiplexer_13_out_4));
  Multiplexer multiplexer_14 (
    .in_1(alu_1_out1), .in_2(data_ram_1_output_1), .in_3(or_4_out), .out_4(multiplexer_14_out_4));
  Data_ram data_ram_1 (
    .Output_1(data_ram_1_output_1), .Output_2(data_ram_1_output_2), .Output_3(data_ram_1_output_3),
    .Output_4(data_ram_1_output_4), .Address_1(or_6_out), .Data_1(and_29_out), .Data_2(and_28_out),
    .Data_3(and_27_out), .Data_4(and_26_out), .Clock(and_7_out), .Read(big_man_cu_1_memread),
    .Write(big_man_cu_1_setaddress));
  or or_6 (or_6_out, and_19_out, and_21_out);

  // Notes on the sheet:
  //   Name: Louis Stalet & Mark Maroun
  //   Id: 261079468 & 261115147
  //   Adder
  //   Program Counter
  //   Input instructions
  //   CU
  //   Instruction RAM
  //   To Instruction Register
  //   Load
  //   Save
  //   Add
  //   Sub
  //   IR
  //   Left
  //   Right
  //   ALU
  //   Data Ram
endmodule

module Instructions_ram (
  input  Mode,
  input  Address_1,
  input  Address_2,
  input  Address_3,
  input  Data_1,
  input  Data_2,
  input  Data_3,
  input  Data_4,
  input  Clock,
  output Output_1,
  output Output_2,
  output Output_3,
  output Output_4
);

  wire Address_0_q, Address_3_q, Address_4_q, Address_5_q, Address_6_q, Address_7_q, and_1_out, and_2_out,
       and_3_out, and_4_out, and_5_out, and_6_out, and_7_out, and_8_out, and_9_out, and_10_out, and_11_out,
       and_12_out, and_13_out, and_14_out, and_15_out, and_16_out, and_17_out, and_18_out, and_19_out,
       and_20_out, and_21_out, and_22_out, and_23_out, and_24_out, and_25_out, and_26_out, and_27_out,
       and_28_out, and_29_out, and_30_out, and_31_out, and_32_out, and_33_out, and_34_out, and_35_out,
       and_36_out, and_37_out, and_38_out, and_39_out, and_40_out, and_41_out, and_42_out, and_43_out,
       and_44_out, and_45_out, and_46_out, and_47_out, and_48_out, d_ff_1_q, d_ff_2_q, d_ff_3_q, d_ff_4_q,
       d_ff_5_q, d_ff_6_q, d_ff_7_q, d_ff_8_q, d_ff_9_q, d_ff_10_q, d_ff_11_q, d_ff_12_q, d_ff_13_q,
       d_ff_14_q, d_ff_15_q, d_ff_16_q, d_ff_17_q, d_ff_18_q, d_ff_19_q, d_ff_20_q, d_ff_21_q, d_ff_22_q,
       d_ff_23_q, d_ff_24_q, d_ff_25_q, d_ff_26_q, d_ff_27_q, d_ff_28_q, d_ff_29_q, Data_register_q,
       not_1_out, not_2_out, not_3_out, not_4_out;

  D_Flip_Flop d_ff_1 (.D(Data_1), .clk(Clock), .Q(d_ff_1_q));  // open: Qn, preset, reset
  D_Flip_Flop d_ff_2 (.D(Data_2), .clk(Clock), .Q(d_ff_2_q));  // open: Qn, preset, reset
  D_Flip_Flop d_ff_3 (.D(Data_3), .clk(Clock), .Q(d_ff_3_q));  // open: Qn, preset, reset
  D_Flip_Flop Data_register (.D(Data_4), .clk(Clock), .Q(Data_register_q));  // open: Qn, preset, reset
  not not_1 (not_1_out, Address_3);
  not not_2 (not_2_out, Address_2);
  not not_3 (not_3_out, Address_1);
  not not_4 (not_4_out, Mode);
  and and_1 (and_1_out, not_1_out, not_2_out, not_3_out);
  and and_2 (and_2_out, not_1_out, not_2_out, Address_1);
  and and_3 (and_3_out, not_1_out, Address_2, not_3_out);
  and and_4 (and_4_out, not_1_out, Address_2, Address_1);
  and and_5 (and_5_out, Address_3, not_2_out, not_3_out);
  and and_6 (and_6_out, Address_3, not_2_out, Address_1);
  and and_7 (and_7_out, Address_3, Address_2, not_3_out);
  and and_8 (and_8_out, Address_3, Address_2, Address_1);
  and and_9 (and_9_out, Address_0_q, and_1_out, Mode, Clock);
  and and_10 (and_10_out, not_4_out, and_1_out, Clock);
  or or_1 (Output_1, and_9_out, and_14_out, and_21_out, and_24_out, and_29_out, and_34_out, and_39_out, and_45_out);
  and and_11 (and_11_out, d_ff_4_q, and_1_out, Mode, Clock);
  D_Flip_Flop Address_0 (.D(d_ff_1_q), .clk(and_10_out), .Q(Address_0_q));  // open: Qn, preset, reset
  D_Flip_Flop d_ff_4 (.D(d_ff_2_q), .clk(and_10_out), .Q(d_ff_4_q));  // open: Qn, preset, reset
  D_Flip_Flop d_ff_5 (.D(d_ff_3_q), .clk(and_10_out), .Q(d_ff_5_q));  // open: Qn, preset, reset
  D_Flip_Flop d_ff_6 (.D(Data_register_q), .clk(and_10_out), .Q(d_ff_6_q));  // open: Qn, preset, reset
  and and_12 (and_12_out, d_ff_5_q, and_1_out, Mode, Clock);
  and and_13 (and_13_out, d_ff_6_q, and_1_out, Mode, Clock);
  and and_14 (and_14_out, d_ff_7_q, and_2_out, Mode, Clock);
  D_Flip_Flop d_ff_7 (.D(d_ff_1_q), .clk(and_15_out), .Q(d_ff_7_q));  // open: Qn, preset, reset
  D_Flip_Flop d_ff_8 (.D(d_ff_2_q), .clk(and_15_out), .Q(d_ff_8_q));  // open: Qn, preset, reset
  D_Flip_Flop d_ff_9 (.D(d_ff_3_q), .clk(and_15_out), .Q(d_ff_9_q));  // open: Qn, preset, reset
  D_Flip_Flop d_ff_10 (.D(Data_register_q), .clk(and_15_out), .Q(d_ff_10_q));  // open: Qn, preset, reset
  and and_15 (and_15_out, not_4_out, and_2_out, Clock);
  or or_2 (Output_2, and_11_out, and_16_out, and_20_out, and_27_out, and_31_out, and_36_out, and_41_out, and_46_out);
  and and_16 (and_16_out, d_ff_8_q, and_2_out, Mode, Clock);
  and and_17 (and_17_out, d_ff_9_q, and_2_out, Mode, Clock);
  and and_18 (and_18_out, d_ff_10_q, and_2_out, Mode, Clock);
  and and_19 (and_19_out, not_4_out, and_3_out, Clock);
  and and_20 (and_20_out, d_ff_12_q, and_3_out, Mode, Clock);
  and and_21 (and_21_out, d_ff_11_q, and_3_out, Mode, Clock);
  D_Flip_Flop d_ff_11 (.D(d_ff_1_q), .clk(and_19_out), .Q(d_ff_11_q));  // open: Qn, preset, reset
  D_Flip_Flop d_ff_12 (.D(d_ff_2_q), .clk(and_19_out), .Q(d_ff_12_q));  // open: Qn, preset, reset
  D_Flip_Flop d_ff_13 (.D(d_ff_3_q), .clk(and_19_out), .Q(d_ff_13_q));  // open: Qn, preset, reset
  D_Flip_Flop d_ff_14 (.D(Data_register_q), .clk(and_19_out), .Q(d_ff_14_q));  // open: Qn, preset, reset
  or or_3 (Output_3, and_12_out, and_17_out, and_22_out, and_26_out, and_32_out, and_37_out, and_42_out, and_47_out);
  and and_22 (and_22_out, d_ff_13_q, and_3_out, Mode, Clock);
  and and_23 (and_23_out, d_ff_14_q, and_3_out, Mode, Clock);
  and and_24 (and_24_out, Address_3_q, and_4_out, Mode, Clock);
  D_Flip_Flop u_Address_3 (.D(d_ff_1_q), .clk(and_25_out), .Q(Address_3_q));  // open: Qn, preset, reset
  D_Flip_Flop d_ff_15 (.D(d_ff_2_q), .clk(and_25_out), .Q(d_ff_15_q));  // open: Qn, preset, reset
  D_Flip_Flop d_ff_16 (.D(d_ff_3_q), .clk(and_25_out), .Q(d_ff_16_q));  // open: Qn, preset, reset
  D_Flip_Flop d_ff_17 (.D(Data_register_q), .clk(and_25_out), .Q(d_ff_17_q));  // open: Qn, preset, reset
  and and_25 (and_25_out, not_4_out, and_4_out, Clock);
  and and_26 (and_26_out, d_ff_16_q, and_4_out, Mode, Clock);
  and and_27 (and_27_out, d_ff_15_q, and_4_out, Mode, Clock);
  or or_4 (Output_4, and_13_out, and_18_out, and_23_out, and_28_out, and_33_out, and_38_out, and_43_out, and_48_out);
  and and_28 (and_28_out, d_ff_17_q, and_4_out, Mode, Clock);
  and and_29 (and_29_out, Address_4_q, and_5_out, Mode, Clock);
  D_Flip_Flop Address_4 (.D(d_ff_1_q), .clk(and_30_out), .Q(Address_4_q));  // open: Qn, preset, reset
  D_Flip_Flop d_ff_18 (.D(d_ff_2_q), .clk(and_30_out), .Q(d_ff_18_q));  // open: Qn, preset, reset
  D_Flip_Flop d_ff_19 (.D(d_ff_3_q), .clk(and_30_out), .Q(d_ff_19_q));  // open: Qn, preset, reset
  D_Flip_Flop d_ff_20 (.D(Data_register_q), .clk(and_30_out), .Q(d_ff_20_q));  // open: Qn, preset, reset
  and and_30 (and_30_out, not_4_out, and_5_out, Clock);
  and and_31 (and_31_out, d_ff_18_q, and_5_out, Mode, Clock);
  and and_32 (and_32_out, d_ff_19_q, and_5_out, Mode, Clock);
  and and_33 (and_33_out, d_ff_20_q, and_5_out, Mode, Clock);
  and and_34 (and_34_out, Address_5_q, and_6_out, Mode, Clock);
  D_Flip_Flop Address_5 (.D(d_ff_1_q), .clk(and_35_out), .Q(Address_5_q));  // open: Qn, preset, reset
  D_Flip_Flop d_ff_21 (.D(d_ff_2_q), .clk(and_35_out), .Q(d_ff_21_q));  // open: Qn, preset, reset
  D_Flip_Flop d_ff_22 (.D(d_ff_3_q), .clk(and_35_out), .Q(d_ff_22_q));  // open: Qn, preset, reset
  D_Flip_Flop d_ff_23 (.D(Data_register_q), .clk(and_35_out), .Q(d_ff_23_q));  // open: Qn, preset, reset
  and and_35 (and_35_out, not_4_out, and_6_out, Clock);
  and and_36 (and_36_out, d_ff_21_q, and_6_out, Mode, Clock);
  and and_37 (and_37_out, d_ff_22_q, and_6_out, Mode, Clock);
  and and_38 (and_38_out, d_ff_23_q, and_6_out, Mode, Clock);
  and and_39 (and_39_out, Address_6_q, and_7_out, Mode, Clock);
  D_Flip_Flop Address_6 (.D(d_ff_1_q), .clk(and_40_out), .Q(Address_6_q));  // open: Qn, preset, reset
  D_Flip_Flop d_ff_24 (.D(d_ff_2_q), .clk(and_40_out), .Q(d_ff_24_q));  // open: Qn, preset, reset
  D_Flip_Flop d_ff_25 (.D(d_ff_3_q), .clk(and_40_out), .Q(d_ff_25_q));  // open: Qn, preset, reset
  D_Flip_Flop d_ff_26 (.D(Data_register_q), .clk(and_40_out), .Q(d_ff_26_q));  // open: Qn, preset, reset
  and and_40 (and_40_out, not_4_out, and_7_out, Clock);
  and and_41 (and_41_out, d_ff_24_q, and_7_out, Mode, Clock);
  and and_42 (and_42_out, d_ff_25_q, and_7_out, Mode, Clock);
  and and_43 (and_43_out, d_ff_26_q, and_7_out, Mode, Clock);
  and and_44 (and_44_out, not_4_out, and_8_out, Clock);
  and and_45 (and_45_out, Address_7_q, and_8_out, Mode, Clock);
  and and_46 (and_46_out, d_ff_27_q, and_8_out, Mode, Clock);
  D_Flip_Flop Address_7 (.D(d_ff_1_q), .clk(and_44_out), .Q(Address_7_q));  // open: Qn, preset, reset
  D_Flip_Flop d_ff_27 (.D(d_ff_2_q), .clk(and_44_out), .Q(d_ff_27_q));  // open: Qn, preset, reset
  D_Flip_Flop d_ff_28 (.D(d_ff_3_q), .clk(and_44_out), .Q(d_ff_28_q));  // open: Qn, preset, reset
  D_Flip_Flop d_ff_29 (.D(Data_register_q), .clk(and_44_out), .Q(d_ff_29_q));  // open: Qn, preset, reset
  and and_47 (and_47_out, d_ff_28_q, and_8_out, Mode, Clock);
  and and_48 (and_48_out, d_ff_29_q, and_8_out, Mode, Clock);
endmodule

module Data_ram (
  input  Write,
  input  Read,
  input  Address_1,
  input  Data_1,
  input  Data_2,
  input  Data_3,
  input  Data_4,
  input  Clock,
  output Output_1,
  output Output_2,
  output Output_3,
  output Output_4
);

  wire Add_register_q, Address_0_q, and_1_out, and_2_out, and_3_out, and_4_out, and_5_out, and_6_out,
       and_7_out, and_8_out, and_9_out, and_10_out, d_ff_1_q, d_ff_2_q, d_ff_3_q, d_ff_4_q, d_ff_5_q,
       d_ff_6_q, d_ff_7_q, d_ff_8_q, not_1_out, or_1_out, or_2_out, or_3_out, or_4_out;

  D_Flip_Flop Add_register (.D(Address_1), .clk(Clock), .Q(Add_register_q));  // open: Qn, preset, reset
  D_Flip_Flop d_ff_1 (.D(Write), .clk(Clock), .Q(d_ff_1_q));  // open: Qn, preset, reset
  not not_1 (not_1_out, Add_register_q);
  and and_1 (and_1_out, Address_0_q, not_1_out, Read, Clock);
  and and_2 (and_2_out, d_ff_1_q, not_1_out, Clock);
  or or_1 (or_1_out, and_1_out, and_6_out);
  and and_3 (and_3_out, d_ff_2_q, not_1_out, Read, Clock);
  D_Flip_Flop Address_0 (.D(Data_1), .clk(and_2_out), .Q(Address_0_q));  // open: Qn, preset, reset
  D_Flip_Flop d_ff_2 (.D(Data_2), .clk(and_2_out), .Q(d_ff_2_q));  // open: Qn, preset, reset
  D_Flip_Flop d_ff_3 (.D(Data_3), .clk(and_2_out), .Q(d_ff_3_q));  // open: Qn, preset, reset
  D_Flip_Flop d_ff_4 (.D(Data_4), .clk(and_2_out), .Q(d_ff_4_q));  // open: Qn, preset, reset
  and and_4 (and_4_out, d_ff_4_q, not_1_out, Read, Clock);
  and and_5 (and_5_out, d_ff_3_q, not_1_out, Read, Clock);
  and and_6 (and_6_out, d_ff_5_q, Add_register_q, Read, Clock);
  D_Flip_Flop d_ff_5 (.D(Data_1), .clk(and_7_out), .Q(d_ff_5_q));  // open: Qn, preset, reset
  D_Flip_Flop d_ff_6 (.D(Data_2), .clk(and_7_out), .Q(d_ff_6_q));  // open: Qn, preset, reset
  D_Flip_Flop d_ff_7 (.D(Data_3), .clk(and_7_out), .Q(d_ff_7_q));  // open: Qn, preset, reset
  D_Flip_Flop d_ff_8 (.D(Data_4), .clk(and_7_out), .Q(d_ff_8_q));  // open: Qn, preset, reset
  and and_7 (and_7_out, d_ff_1_q, Add_register_q, Clock);
  or or_2 (or_2_out, and_3_out, and_8_out);
  and and_8 (and_8_out, d_ff_6_q, Add_register_q, Read, Clock);
  and and_9 (and_9_out, d_ff_7_q, Add_register_q, Read, Clock);
  and and_10 (and_10_out, d_ff_8_q, Add_register_q, Read, Clock);
  or or_3 (or_3_out, and_5_out, and_9_out);
  or or_4 (or_4_out, and_4_out, and_10_out);
  D_Flip_Flop #(.trigger("falling")) Out_register (.D(or_1_out), .clk(Clock), .Q(Output_1));  // open: Qn, preset, reset
  D_Flip_Flop #(.trigger("falling")) d_ff_9 (.D(or_2_out), .clk(Clock), .Q(Output_2));  // open: Qn, preset, reset
  D_Flip_Flop #(.trigger("falling")) d_ff_10 (.D(or_3_out), .clk(Clock), .Q(Output_3));  // open: Qn, preset, reset
  D_Flip_Flop #(.trigger("falling")) d_ff_11 (.D(or_4_out), .clk(Clock), .Q(Output_4));  // open: Qn, preset, reset
endmodule

module ALU (
  input  Clock,
  input  L_input4,
  input  L_input3,
  input  L_input2,
  input  L_input1,
  input  R_input4,
  input  R_input3,
  input  R_input2,
  input  R_input1,
  input  Add_Sub,
  output Neg_status,
  output Zero_status,
  output Magnitude_Overflow_status,
  output Signed_Overflow_satus,
  output out4,
  output out3,
  output out2,
  output out1
);

  wire and_1_out, and_2_out, and_3_out, and_4_out, and_5_out, and_6_out, and_7_out, and_8_out, and_9_out,
       and_10_out, and_11_out, and_12_out, and_13_out, and_14_out, d_ff_1_q, d_ff_3_q, d_ff_5_q, d_ff_7_q,
       d_ff_9_q, d_ff_10_q, d_ff_11_q, d_ff_12_q, d_ff_13_q, nand_1_out, nand_2_out, nand_3_out, nand_4_out,
       nor_1_out, not_1_out, or_1_out, or_2_out, or_3_out, or_4_out, or_5_out, or_6_out, or_7_out, xor_1_out,
       xor_2_out, xor_3_out, xor_4_out, xor_5_out, xor_6_out, xor_7_out, xor_8_out, xor_9_out, xor_10_out,
       xor_11_out, xor_12_out;

  D_Flip_Flop d_ff_1 (.D(Add_Sub), .clk(Clock), .Q(d_ff_1_q));  // open: Qn, preset, reset
  or or_1 (or_1_out, and_1_out, and_2_out);
  and and_1 (and_1_out, d_ff_3_q, or_4_out);
  and and_2 (and_2_out, xor_1_out, or_2_out);
  D_Flip_Flop d_ff_2 (.D(xor_2_out), .clk(Clock), .Q(out4));  // open: Qn, preset, reset
  D_Flip_Flop d_ff_3 (.D(L_input4), .clk(Clock), .Q(d_ff_3_q));  // open: Qn, preset, reset
  xor xor_1 (xor_1_out, d_ff_3_q, or_4_out);
  or or_2 (or_2_out, and_3_out, and_4_out);
  xor xor_2 (xor_2_out, xor_1_out, or_2_out);
  D_Flip_Flop d_ff_4 (.D(xor_4_out), .clk(Clock), .Q(out3));  // open: Qn, preset, reset
  D_Flip_Flop d_ff_5 (.D(L_input3), .clk(Clock), .Q(d_ff_5_q));  // open: Qn, preset, reset
  and and_3 (and_3_out, d_ff_5_q, or_5_out);
  and and_4 (and_4_out, xor_3_out, or_3_out);
  D_Flip_Flop d_ff_6 (.D(xor_6_out), .clk(Clock), .Q(out2));  // open: Qn, preset, reset
  D_Flip_Flop d_ff_7 (.D(L_input2), .clk(Clock), .Q(d_ff_7_q));  // open: Qn, preset, reset
  xor xor_3 (xor_3_out, d_ff_5_q, or_5_out);
  xor xor_4 (xor_4_out, xor_3_out, or_3_out);
  D_Flip_Flop d_ff_8 (.D(xor_7_out), .clk(Clock), .Q(out1));  // open: Qn, preset, reset
  D_Flip_Flop d_ff_9 (.D(L_input1), .clk(Clock), .Q(d_ff_9_q));  // open: Qn, preset, reset
  and and_5 (and_5_out, d_ff_7_q, or_6_out);
  or or_3 (or_3_out, and_5_out, and_6_out);
  xor xor_5 (xor_5_out, d_ff_7_q, or_6_out);
  and and_6 (and_6_out, xor_5_out, and_7_out);
  and and_7 (and_7_out, d_ff_9_q, or_7_out);
  xor xor_6 (xor_6_out, xor_5_out, and_7_out);
  xor xor_7 (xor_7_out, d_ff_9_q, or_7_out);
  D_Flip_Flop d_ff_10 (.D(R_input4), .clk(Clock), .Q(d_ff_10_q));  // open: Qn, preset, reset
  D_Flip_Flop d_ff_11 (.D(R_input3), .clk(Clock), .Q(d_ff_11_q));  // open: Qn, preset, reset
  D_Flip_Flop d_ff_12 (.D(R_input2), .clk(Clock), .Q(d_ff_12_q));  // open: Qn, preset, reset
  D_Flip_Flop d_ff_13 (.D(R_input1), .clk(Clock), .Q(d_ff_13_q));  // open: Qn, preset, reset
  not not_1 (not_1_out, d_ff_1_q);
  nor nor_1 (nor_1_out, out4, out3, out2, out1);
  xor xor_8 (xor_8_out, or_1_out, or_2_out);
  and and_8 (and_8_out, d_ff_10_q, not_1_out);
  and and_9 (and_9_out, d_ff_11_q, not_1_out);
  D_Flip_Flop d_ff_14 (.D(out4), .clk(Clock), .Q(Neg_status));  // open: Qn, preset, reset
  D_Flip_Flop d_ff_15 (.D(nor_1_out), .clk(Clock), .Q(Zero_status));  // open: Qn, preset, reset
  D_Flip_Flop d_ff_16 (.D(or_1_out), .clk(Clock), .Q(Magnitude_Overflow_status));  // open: Qn, preset, reset
  D_Flip_Flop d_ff_17 (.D(xor_8_out), .clk(Clock), .Q(Signed_Overflow_satus));  // open: Qn, preset, reset
  nand nand_1 (nand_1_out, d_ff_13_q, d_ff_1_q);
  nand nand_2 (nand_2_out, d_ff_12_q, d_ff_1_q);
  nand nand_3 (nand_3_out, d_ff_11_q, d_ff_1_q);
  nand nand_4 (nand_4_out, d_ff_10_q, d_ff_1_q);
  and and_10 (and_10_out, d_ff_12_q, not_1_out);
  or or_4 (or_4_out, and_8_out, xor_12_out);
  and and_11 (and_11_out, d_ff_13_q, not_1_out);
  or or_5 (or_5_out, and_9_out, xor_11_out);
  or or_6 (or_6_out, and_10_out, xor_10_out);
  or or_7 (or_7_out, and_11_out, xor_9_out);
  xor xor_9 (xor_9_out, 1'b1, nand_1_out);
  and and_12 (and_12_out, 1'b1, nand_1_out);
  and and_13 (and_13_out, and_12_out, nand_2_out);
  xor xor_10 (xor_10_out, and_12_out, nand_2_out);
  xor xor_11 (xor_11_out, and_13_out, nand_3_out);
  and and_14 (and_14_out, and_13_out, nand_3_out);
  xor xor_12 (xor_12_out, and_14_out, nand_4_out);

  // Notes on the sheet:
  //   Full adder
  //   L_input
  //   A_out
  //   R_input
  //   Status derermination
  //   2's Complement
  //   Status_Out
endmodule

module Multiplexer (
  input  in_1,
  input  in_2,
  input  in_3,
  output out_4
);

  wire and_1_out, and_2_out, not_1_out;

  not not_1 (not_1_out, in_3);
  and and_1 (and_1_out, in_3, in_1);
  or or_1 (out_4, and_1_out, and_2_out);
  and and_2 (and_2_out, not_1_out, in_2);
endmodule

module adder (
  input  in_1,
  input  in_2,
  input  in_3,
  output out_4,
  output out_5,
  output out_6,
  output out_7
);

  wire and_1_out, and_2_out, and_3_out, and_4_out, and_5_out, or_2_out, xor_1_out, xor_3_out;

  or or_1 (out_4, and_1_out, and_2_out);
  and and_1 (and_1_out, in_1, 1'b0);
  and and_2 (and_2_out, xor_1_out, or_2_out);
  xor xor_1 (xor_1_out, in_1, 1'b0);
  xor xor_2 (out_5, xor_1_out, or_2_out);
  and and_3 (and_3_out, in_2, 1'b0);
  or or_2 (or_2_out, and_3_out, and_4_out);
  xor xor_3 (xor_3_out, in_2, 1'b0);
  and and_4 (and_4_out, xor_3_out, and_5_out);
  and and_5 (and_5_out, in_3, 1'b1);
  xor xor_4 (out_6, xor_3_out, and_5_out);
  xor xor_5 (out_7, in_3, 1'b1);

  // Notes on the sheet:
  //   Full adder
  //   A_out
endmodule

module Register_blck (
  input  Data_input4,
  input  Data_input3,
  input  Data_input2,
  input  Data_input1,
  input  Load,
  input  Save,
  input  register_choice,
  input  Bothregister_flag,
  input  Clock,
  output output4,
  output output3,
  output output2,
  output output1,
  output output4_2,
  output output3_2,
  output output2_2,
  output output1_2
);

  wire and_1_out, and_2_out, and_3_out, and_4_out, and_5_out, and_6_out, and_7_out, and_8_out, and_9_out,
       and_10_out, d_ff_1_q, d_ff_2_q, d_ff_3_q, d_ff_4_q, d_ff_5_q, d_ff_6_q, d_ff_7_q, d_ff_8_q, d_ff_9_q,
       d_ff_10_q, d_ff_11_q, d_ff_12_q, not_1_out, or_1_out, or_2_out;

  D_Flip_Flop d_ff_1 (.D(Data_input4), .clk(Clock), .Q(d_ff_1_q));  // open: Qn, preset, reset
  D_Flip_Flop d_ff_2 (.D(Data_input3), .clk(Clock), .Q(d_ff_2_q));  // open: Qn, preset, reset
  D_Flip_Flop d_ff_3 (.D(Data_input2), .clk(Clock), .Q(d_ff_3_q));  // open: Qn, preset, reset
  D_Flip_Flop d_ff_4 (.D(Data_input1), .clk(Clock), .Q(d_ff_4_q));  // open: Qn, preset, reset
  D_Flip_Flop d_ff_5 (.D(d_ff_1_q), .clk(and_1_out), .Q(d_ff_5_q));  // open: Qn, preset, reset
  D_Flip_Flop d_ff_6 (.D(d_ff_1_q), .clk(and_2_out), .Q(d_ff_6_q));  // open: Qn, preset, reset
  and and_1 (and_1_out, ~register_choice, Load, Clock);  // AND_Gate
  and and_2 (and_2_out, register_choice, Load, Clock);
  D_Flip_Flop d_ff_7 (.D(d_ff_2_q), .clk(and_1_out), .Q(d_ff_7_q));  // open: Qn, preset, reset
  D_Flip_Flop d_ff_8 (.D(d_ff_2_q), .clk(and_2_out), .Q(d_ff_8_q));  // open: Qn, preset, reset
  D_Flip_Flop d_ff_9 (.D(d_ff_3_q), .clk(and_1_out), .Q(d_ff_9_q));  // open: Qn, preset, reset
  D_Flip_Flop d_ff_10 (.D(d_ff_3_q), .clk(and_2_out), .Q(d_ff_10_q));  // open: Qn, preset, reset
  not not_1 (not_1_out, register_choice);
  or or_1 (or_1_out, register_choice, Bothregister_flag);
  D_Flip_Flop d_ff_11 (.D(d_ff_4_q), .clk(and_1_out), .Q(d_ff_11_q));  // open: Qn, preset, reset
  D_Flip_Flop d_ff_12 (.D(d_ff_4_q), .clk(and_2_out), .Q(d_ff_12_q));  // open: Qn, preset, reset
  or or_2 (or_2_out, not_1_out, Bothregister_flag);
  and and_3 (and_3_out, Clock, Save, or_2_out, d_ff_5_q);
  and and_4 (and_4_out, Clock, Save, or_2_out, d_ff_7_q);
  and and_5 (and_5_out, Clock, Save, or_2_out, d_ff_9_q);
  and and_6 (and_6_out, Clock, Save, or_2_out, d_ff_11_q);
  and and_7 (and_7_out, Clock, Save, or_1_out, d_ff_6_q);
  and and_8 (and_8_out, Clock, Save, or_1_out, d_ff_8_q);
  and and_9 (and_9_out, Clock, Save, or_1_out, d_ff_10_q);
  and and_10 (and_10_out, Clock, Save, or_1_out, d_ff_12_q);
  D_Flip_Flop #(.trigger("falling")) d_ff_13 (.D(and_3_out), .clk(Clock), .Q(output4));  // open: Qn, preset, reset
  D_Flip_Flop #(.trigger("falling")) d_ff_14 (.D(and_4_out), .clk(Clock), .Q(output3));  // open: Qn, preset, reset
  D_Flip_Flop #(.trigger("falling")) d_ff_15 (.D(and_5_out), .clk(Clock), .Q(output2));  // open: Qn, preset, reset
  D_Flip_Flop #(.trigger("falling")) d_ff_16 (.D(and_6_out), .clk(Clock), .Q(output1));  // open: Qn, preset, reset
  D_Flip_Flop #(.trigger("falling")) d_ff_17 (.D(and_7_out), .clk(Clock), .Q(output4_2));  // open: Qn, preset, reset
  D_Flip_Flop #(.trigger("falling")) d_ff_18 (.D(and_8_out), .clk(Clock), .Q(output3_2));  // open: Qn, preset, reset
  D_Flip_Flop #(.trigger("falling")) d_ff_19 (.D(and_9_out), .clk(Clock), .Q(output2_2));  // open: Qn, preset, reset
  D_Flip_Flop #(.trigger("falling")) d_ff_20 (.D(and_10_out), .clk(Clock), .Q(output1_2));  // open: Qn, preset, reset

  // Notes on the sheet:
  //   Data Ram Output
  //   R0
  //   R1
endmodule

module Decoder (
  input  Input,
  input  Selector,
  output out_3,
  output out_4
);

  wire and_2_out, not_1_out, not_2_out;

  not not_1 (not_1_out, Input);
  not not_2 (not_2_out, not_1_out);
  and and_1 (out_3, not_2_out, Selector);
  not not_3 (out_4, and_2_out);
  and and_2 (and_2_out, not_1_out, Selector);
endmodule

module multiplexerX4 (
  input  out1_1,
  input  out1_2,
  input  out1_3,
  input  out1_4,
  input  out2_1,
  input  out2_2,
  input  out2_3,
  input  out2_4,
  input  in_9,
  output out4,
  output out3,
  output out2,
  output out1
);

  Multiplexer multiplexer_1 (.in_1(out2_1), .in_2(out1_1), .in_3(in_9), .out_4(out1));
  Multiplexer multiplexer_2 (.in_1(out2_2), .in_2(out1_2), .in_3(in_9), .out_4(out2));
  Multiplexer multiplexer_3 (.in_1(out2_3), .in_2(out1_3), .in_3(in_9), .out_4(out3));
  Multiplexer multiplexer_4 (.in_1(out2_4), .in_2(out1_4), .in_3(in_9), .out_4(out4));
endmodule

module big_man_CU (
  input  in_4,
  input  in_3,
  input  in_2,
  input  in_1,
  input  in_5,
  output RegRead,
  output SetAddress,
  output memWrite,
  output RegWrite,
  output memRead,
  output incr_pc,
  output PCoRAM,
  output RAMtoIR,
  output ALUop,
  output HALT,
  output reset_ir
);

  wire addToR0_out, addToR1_out, and_1_out, and_2_out, and_3_out, and_4_out, and_6_out, and_7_out, and_8_out,
       and_9_out, and_10_out, and_11_out, and_12_out, and_13_out, and_14_out, and_15_out, and_16_out,
       and_17_out, and_18_out, and_19_out, and_20_out, and_21_out, and_22_out, and_23_out, and_24_out,
       and_25_out, and_26_out, and_27_out, and_28_out, and_29_out, and_30_out, and_31_out, and_32_out,
       and_33_out, and_34_out, and_35_out, and_36_out, and_38_out, and_39_out, and_40_out, and_41_out,
       and_42_out, and_43_out, and_44_out, and_45_out, and_46_out, and_47_out, d_ff_1_q, d_ff_2_q, d_ff_3_q,
       d_ff_4_q, d_ff_5_q, d_ff_6_q, d_ff_7_q, d_ff_8_q, d_ff_9_q, Execute, Load_R0_out, Load_R1_out,
       nor_1_out, nor_2_out, not_1_out, not_2_out, not_3_out, not_4_out, not_5_out, not_6_out, not_7_out,
       not_8_out, not_9_out, not_10_out, or_1_out, or_10_out, Save_R0_out, Save_R1_out, SubToR0_out,
       SubToR1_out;

  nor nor_1 (nor_1_out, incr_pc, nor_2_out);
  nor nor_2 (nor_2_out, nor_1_out, and_39_out);
  D_Flip_Flop d_ff_1 (.D(nor_1_out), .clk(in_5), .Q(d_ff_1_q));  // open: Qn, preset, reset
  D_Flip_Flop d_ff_2 (.D(in_4), .clk(in_5), .Q(d_ff_2_q));  // open: Qn, preset, reset
  D_Flip_Flop d_ff_3 (.D(in_3), .clk(in_5), .Q(d_ff_3_q));  // open: Qn, preset, reset
  D_Flip_Flop d_ff_4 (.D(in_2), .clk(in_5), .Q(d_ff_4_q));  // open: Qn, preset, reset
  and and_1 (and_1_out, ~d_ff_2_q, ~d_ff_3_q);  // AND_Gate
  and and_2 (and_2_out, ~d_ff_2_q, d_ff_3_q);  // AND_Gate
  and and_3 (and_3_out, d_ff_2_q, ~d_ff_3_q);  // AND_Gate
  and and_4 (and_4_out, d_ff_2_q, d_ff_3_q);
  and and_5 (HALT, d_ff_2_q, d_ff_3_q, d_ff_4_q, d_ff_5_q);
  D_Flip_Flop d_ff_5 (.D(in_1), .clk(in_5), .Q(d_ff_5_q));  // open: Qn, preset, reset
  D_Flip_Flop d_ff_6 (.D(not_2_out), .clk(in_5), .Q(d_ff_6_q), .reset(d_ff_9_q));  // open: Qn, preset
  D_Flip_Flop d_ff_7 (.D(not_3_out), .clk(not_2_out), .Q(d_ff_7_q), .reset(d_ff_9_q));  // open: Qn, preset
  D_Flip_Flop d_ff_8 (.D(not_4_out), .clk(not_3_out), .Q(d_ff_8_q), .reset(d_ff_9_q));  // open: Qn, preset
  D_Flip_Flop #(.trigger("falling")) d_ff_9 (.D(Execute), .clk(in_5), .Q(d_ff_9_q));  // open: Qn, preset, reset
  not not_1 (not_1_out, d_ff_1_q);
  and Load_R0 (Load_R0_out, d_ff_1_q, ~d_ff_4_q, and_1_out);  // AND_Gate
  and Load_R1 (Load_R1_out, d_ff_1_q, d_ff_4_q, and_1_out);
  and Save_R0 (Save_R0_out, d_ff_1_q, ~d_ff_4_q, and_2_out);  // AND_Gate
  and Save_R1 (Save_R1_out, d_ff_1_q, d_ff_4_q, and_2_out);
  and addToR0 (addToR0_out, and_3_out, ~d_ff_4_q, d_ff_1_q);  // AND_Gate
  and addToR1 (addToR1_out, and_3_out, d_ff_4_q, d_ff_1_q);
  and SubToR0 (SubToR0_out, and_4_out, ~d_ff_4_q, d_ff_1_q);  // AND_Gate
  and SubToR1 (SubToR1_out, and_4_out, d_ff_4_q, d_ff_1_q);
  not not_2 (not_2_out, d_ff_6_q);
  not not_3 (not_3_out, d_ff_7_q);
  not not_4 (not_4_out, d_ff_8_q);
  and and_6 (and_6_out, not_1_out, in_5);
  not not_5 (not_5_out, not_2_out);
  not not_6 (not_6_out, not_3_out);
  not not_7 (not_7_out, not_4_out);
  and and_7 (and_7_out, Load_R0_out, and_41_out, d_ff_1_q);
  and and_8 (and_8_out, Load_R0_out, and_42_out, d_ff_1_q);
  and and_9 (and_9_out, Load_R0_out, and_43_out, d_ff_1_q);
  and and_10 (and_10_out, Load_R1_out, and_41_out, d_ff_1_q);
  and and_11 (and_11_out, Load_R1_out, and_42_out, d_ff_1_q);
  and and_12 (and_12_out, Load_R1_out, and_43_out, d_ff_1_q);
  and and_13 (and_13_out, Save_R0_out, and_41_out, d_ff_1_q);
  and and_14 (and_14_out, Save_R0_out, and_42_out, d_ff_1_q);
  and and_15 (and_15_out, Save_R0_out, and_43_out, d_ff_1_q);
  and and_16 (and_16_out, Save_R0_out, and_44_out, d_ff_1_q);
  and and_17 (and_17_out, Save_R1_out, and_41_out, d_ff_1_q);
  and and_18 (and_18_out, Save_R1_out, and_42_out, d_ff_1_q);
  and and_19 (and_19_out, Save_R1_out, and_43_out, d_ff_1_q);
  and and_20 (and_20_out, Save_R1_out, and_44_out, d_ff_1_q);
  and and_21 (and_21_out, addToR0_out, and_41_out, d_ff_1_q);
  and and_22 (and_22_out, addToR0_out, and_42_out, d_ff_1_q);
  and and_23 (and_23_out, addToR0_out, and_43_out, d_ff_1_q);
  and and_24 (and_24_out, addToR0_out, and_44_out, d_ff_1_q);
  and and_25 (and_25_out, addToR1_out, and_41_out, d_ff_1_q);
  and and_26 (and_26_out, addToR1_out, and_42_out, d_ff_1_q);
  and and_27 (and_27_out, addToR1_out, and_43_out, d_ff_1_q);
  and and_28 (and_28_out, addToR1_out, and_44_out, d_ff_1_q);
  and and_29 (and_29_out, SubToR0_out, and_41_out, d_ff_1_q);
  and and_30 (and_30_out, SubToR0_out, and_42_out, d_ff_1_q);
  and and_31 (and_31_out, SubToR0_out, and_43_out, d_ff_1_q);
  and and_32 (and_32_out, SubToR0_out, and_44_out, d_ff_1_q);
  and and_33 (and_33_out, SubToR1_out, and_41_out, d_ff_1_q);
  and and_34 (and_34_out, SubToR1_out, and_42_out, d_ff_1_q);
  and and_35 (and_35_out, SubToR1_out, and_43_out, d_ff_1_q);
  and and_36 (and_36_out, SubToR1_out, and_44_out, d_ff_1_q);
  and and_37 (reset_ir, and_41_out, ~and_42_out, ~and_43_out, and_6_out);  // AND_Gate
  and and_38 (and_38_out, ~and_41_out, and_42_out, ~and_43_out, and_6_out);  // AND_Gate
  and and_39 (and_39_out, ~and_41_out, ~and_42_out, and_43_out, and_6_out);  // AND_Gate
  not not_8 (not_8_out, not_5_out);
  not not_9 (not_9_out, not_6_out);
  not not_10 (not_10_out, not_7_out);
  and and_40 (and_40_out, not_10_out, not_9_out, not_8_out);
  and and_41 (and_41_out, not_10_out, not_9_out, not_5_out);
  and and_42 (and_42_out, not_10_out, not_6_out, not_8_out);
  and and_43 (and_43_out, not_10_out, not_6_out, not_5_out);
  and and_44 (and_44_out, not_7_out, not_9_out, not_8_out);
  and and_45 (and_45_out, not_7_out, not_9_out, not_5_out);
  and and_46 (and_46_out, not_7_out, not_6_out, not_8_out);
  and and_47 (and_47_out, not_7_out, not_6_out, not_5_out);
  or or_1 (or_1_out, reset_ir, and_39_out);
  or or_2 (RegRead, and_13_out, and_29_out, and_18_out, and_25_out, and_21_out, and_14_out, and_33_out, and_17_out);
  or or_3 (SetAddress, and_13_out, and_17_out);
  or or_4 (memWrite, and_13_out, and_17_out);
  or or_5 (memRead, and_7_out, and_10_out);
  or or_6 (incr_pc, and_32_out, and_28_out, and_9_out, and_12_out, and_24_out, and_16_out, and_20_out, and_36_out);
  buf or_7 (RAMtoIR, or_10_out);  // OR_Gate
  or or_8 (Execute, and_36_out, and_24_out, and_39_out, and_9_out, and_28_out, and_12_out, and_16_out, and_20_out, and_32_out);
  or or_9 (ALUop, and_29_out, and_21_out, and_26_out, and_22_out, and_30_out, and_34_out, and_25_out, and_33_out);
  or or_10 (or_10_out, and_38_out, and_39_out);
  or or_11 (RegWrite, and_36_out, and_28_out, and_31_out, and_8_out, and_11_out, and_23_out, and_27_out, and_35_out, and_24_out, and_32_out);
  or or_12 (PCoRAM, and_36_out, and_20_out, and_16_out, or_1_out, and_9_out, and_32_out, or_10_out, and_12_out, and_24_out, and_28_out);

  // Notes on the sheet:
  //   Load
  //   Save
  //   Add
  //   Sub
  //   Halt
  //   Go to RAM
  //   Write R0
  //   incr PC + fetch
  //   Go to RAM
  //   Write R1
  //   incr PC + fetch
  //   read register R0
  //   set addresss
  //   Write to ram
  //   incr PC + Fetch
  //   read register R1
  //   set addresss
  //   Write to ram
  //   incr PC + Fetch
  //   read register
  //   ALUop
  //   Write R0
  //   incr PC + Fetch
  //   Write R1
  //   read register
  //   ALUop
  //   Write R0
  //   incr PC + Fetch
  //   Write R1
  //   read register
  //   ALUop
  //   incr PC + Fetch
  //   read register
  //   ALUop
  //   incr PC + Fetch
  //   pc to instruction ram
  //   ram to IR
endmodule
